// Logisim project cpu.circ as structural Verilog: 1 circuit, main circuit main
module main (
);

  // ALU alu_1: pin names not known
  // main_regs main_regs_1: pin names not known
  // FLAGS_regs flags_regs_1: pin names not known
  // instructionROM instructionrom_1: pin names not known
  // dataRAM dataram_1: pin names not known
endmodule
