// Logisim project memoryProgramCounter.circ as structural Verilog: 1 circuit, main circuit programCounter
module programCounter (
  input  CLK,
  input  [15:0] Jump_Addr,
  input  PC_Load,
  input  Reset,
  output [15:0] Line
);

  wire fulladder8_1_cout;
  wire [15:0] fulladder8_1_sum, multiplexer_1_out;

  Register #(.width(16)) register_1 (.D(multiplexer_1_out), .en(CLK), .clk(CLK), .Q(Line), .clr(Reset));
  Multiplexer #(.width(16)) multiplexer_1 (
    .in0(fulladder8_1_sum), .in1(Jump_Addr), .out(multiplexer_1_out), .sel(PC_Load));
  FullAdder8 fulladder8_1 (
    .b(Line[7:0]), .cin(1'b1), .cout(fulladder8_1_cout), .sum(fulladder8_1_sum[7:0]));  // open: a, cout6
  FullAdder8 fulladder8_2 (
    .b(Line[15:8]), .cin(fulladder8_1_cout), .sum(fulladder8_1_sum[15:8]));  // open: a, cout, cout6
endmodule
